# Fritzing sketch togglButton (saved by Fritzing 0.9.4)
breadboards: 1

parts:
  U3 = NodeMCU V1.0
  S1 = Round Pushbutton
  LED1 = smd LED [color="Red (633nm)" package="0603 [SMD]"]
  R1 = Resistor [tolerance=±5% resistance=10k package="0402 [SMD]"]

nets:
  N1: U3.3V3, S1.leg1
  N2: U3.GND, LED1.cathode, R1.Pin_0
  N3: U3.D5, S1.leg0, R1.Pin_1
  N4: U3.D6, LED1.anode

custom parts:
  NodeMCU V1.0: ESP8266 based NodeMCU
